# Fritzing sketch wemos-neopixel (saved by Fritzing 0.9.3b)
breadboards: 1

parts:
  WeMos_D1_Mini1 = WeMos D1 Mini
  hc-sr1 = hc-sr04
  RGB_SMD_LED1 = SMD RGB LED (WS2812) [package=5050]  # not connected
  LED1 = LED_RING [package=led_ring]  # not connected

nets:
  5V: WeMos_D1_Mini1.5V, hc-sr1.VCC
  N1: WeMos_D1_Mini1.D1, hc-sr1.Trig
  N2: WeMos_D1_Mini1.D2, hc-sr1.Echo
  N3: WeMos_D1_Mini1.G, hc-sr1.GND
