# Fritzing sketch wemos-servo-hc-sr04 (saved by Fritzing 0.9.3b)
breadboards: 1

parts:
  WeMos_D1_Mini1 = WeMos D1 Mini
  hc-sr1 = hc-sr04
  J1 = Basic Servo

nets:
  VCC: WeMos_D1_Mini1.5V, hc-sr1.VCC, J1.vcc
  N1: WeMos_D1_Mini1.D1, hc-sr1.Trig
  N2: WeMos_D1_Mini1.D2, hc-sr1.Echo
  N3: WeMos_D1_Mini1.D3, J1.pulse
  GND: WeMos_D1_Mini1.G, hc-sr1.GND, J1.gnd
